// Logisim project 8bit_CPU_FINAL.circ as structural Verilog: 2 circuits, main circuit main
module main (
);

  wire clock_1_out, cpu_1_clock_out, cpu_1_keyboard_load, cpu_1_ram_write, cpu_1_tty_write, RESET_out;
  wire [6:0] cpu_1_tty_data_output, keyboard_1_data;
  wire [7:0] cpu_1_ram_data_out, ram_1_dout;
  wire [15:0] cpu_1_ram_address;

  RAM #(.addrWidth(16), .enables("line")) ram_1 (
    .addr(cpu_1_ram_address), .we(cpu_1_ram_write), .clk(cpu_1_clock_out), .din(cpu_1_ram_data_out),
    .dout(ram_1_dout));
  Clock clock_1 (.out(clock_1_out));
  CPU cpu_1 (
    .RAM_DATA_IN(ram_1_dout), .clock_in(clock_1_out), .reset(RESET_out), .keyboard_data_in(keyboard_1_data),
    .RAM_DATA_OUT(cpu_1_ram_data_out), .RAM_ADDRESS(cpu_1_ram_address), .RAM_WRITE(cpu_1_ram_write),
    .clock_out(cpu_1_clock_out), .tty_write(cpu_1_tty_write), .tty_data_output(cpu_1_tty_data_output),
    .keyboard_load(cpu_1_keyboard_load));  // open: DATA_BUS_OUTPUT
  TTY tty_1 (.data(cpu_1_tty_data_output), .clk(cpu_1_clock_out), .we(cpu_1_tty_write), .clr(RESET_out));
  Keyboard keyboard_1 (.clk(cpu_1_keyboard_load), .clr(RESET_out), .data(keyboard_1_data));  // open: re, avail
  Button RESET (.out(RESET_out));
endmodule

module CPU (
  input  [7:0] RAM_DATA_IN,
  input  clock_in,
  input  reset,
  input  [6:0] keyboard_data_in,
  output [7:0] RAM_DATA_OUT,
  output [7:0] DATA_BUS_OUTPUT,
  output [15:0] RAM_ADDRESS,
  output RAM_WRITE,
  output clock_out,
  output tty_write,
  output [6:0] tty_data_output,
  output keyboard_load
);

  wire and_1_out, and_2_out, and_3_out, and_4_out, and_5_out, and_6_out, and_7_out, and_8_out, and_9_out,
       and_10_out, and_11_out, and_12_out, and_13_out, and_14_out, and_15_out, and_16_out, and_17_out,
       and_18_out, and_19_out, and_20_out, and_21_out, and_22_out, and_23_out, and_24_out, and_25_out,
       and_26_out, and_27_out, and_28_out, and_29_out, and_30_out, and_31_out, and_32_out, and_33_out,
       and_34_out, and_35_out, and_36_out, and_37_out, and_38_out, and_39_out, and_40_out, and_41_out,
       and_42_out, and_43_out, and_44_out, and_45_out, and_46_out, and_47_out, and_48_out, and_49_out,
       and_50_out, and_51_out, and_52_out, and_53_out, and_54_out, and_55_out, and_56_out, and_57_out,
       and_58_out, and_59_out, and_60_out, and_61_out, and_62_out, and_63_out, and_64_out, and_65_out,
       and_66_out, and_67_out, and_68_out, and_69_out, and_71_out, and_72_out, and_73_out, and_74_out,
       and_75_out, and_76_out, and_77_out, and_78_out, and_79_out, and_80_out, and_81_out, and_82_out,
       and_83_out, and_84_out, and_85_out, and_86_out, and_87_out, and_88_out, and_89_out, and_90_out,
       and_91_out, and_92_out, and_93_out, and_94_out, and_95_out, and_96_out, and_97_out, and_98_out,
       and_99_out, and_100_out, and_101_out, and_102_out, and_103_out, and_104_out, and_105_out, and_106_out,
       and_107_out, and_108_out, and_109_out, and_110_out, and_111_out, and_112_out, and_113_out,
       and_114_out, and_115_out, and_116_out, and_117_out, and_118_out, and_119_out, and_120_out,
       and_121_out, and_122_out, and_123_out, and_124_out, and_125_out, and_126_out, and_127_out,
       and_128_out, and_129_out, and_130_out, and_131_out, and_132_out, and_133_out, and_134_out,
       buffer_1_out, buffer_2_out, buffer_4_out, buffer_6_out, buffer_7_out, buffer_8_out, buffer_9_out,
       buffer_10_out, buffer_11_out, buffer_12_out, buffer_17_out, buffer_18_out, buffer_19_out,
       buffer_22_out, buffer_25_out, buffer_28_out, buffer_29_out, buffer_30_out, buffer_31_out,
       buffer_41_out, buffer_45_out, buffer_48_out, buffer_50_out, buffer_53_out, buffer_54_out,
       buffer_58_out, buffer_63_out, buffer_74_out, buffer_78_out, buffer_94_out, buffer_97_out,
       buffer_103_out, buffer_104_out, buffer_122_out, buffer_124_out, button_1_out, decoder_1_out0,
       decoder_1_out1, decoder_1_out2, decoder_1_out3, decoder_1_out5, decoder_1_out7, decoder_2_out0,
       decoder_2_out1, decoder_2_out2, decoder_2_out3, decoder_3_out0, decoder_3_out1, decoder_3_out2,
       decoder_4_out0, decoder_4_out1, decoder_4_out2, decoder_4_out3, decoder_4_out4, decoder_4_out5,
       decoder_4_out6, decoder_4_out7, decoder_4_out8, decoder_5_out0, decoder_5_out1, decoder_5_out2,
       decoder_5_out3, decoder_5_out4, decoder_5_out5, decoder_5_out6, decoder_5_out7, decoder_5_out8,
       decoder_5_out9, decoder_5_out10, decoder_5_out11, decoder_5_out12, decoder_5_out13, decoder_6_out0,
       decoder_6_out1, decoder_6_out2, decoder_6_out3, decoder_7_out0, decoder_7_out1, decoder_7_out2,
       decoder_7_out3, decoder_7_out4, decoder_7_out5, decoder_8_out0, decoder_8_out1, decoder_8_out2,
       decoder_8_out4, decoder_9_out2, decoder_10_out2, decoder_11_out2, decoder_12_out2, decoder_12_out4,
       decoder_12_out6, decoder_13_out6, decoder_14_out6, decoder_15_out2, decoder_16_out5, decoder_16_out6,
       decoder_17_out6, decoder_18_out6, decoder_20_out6, decoder_21_out6, decoder_22_out6, decoder_22_out7,
       decoder_23_out7, decoder_24_out7, decoder_25_out2, decoder_26_out6, decoder_26_out7, decoder_27_out2,
       decoder_28_out2, decoder_29_out7, decoder_30_out7, decoder_31_out2, decoder_32_out6, decoder_33_out6,
       decoder_34_out2, decoder_35_out5, decoder_35_out6, decoder_35_out7, decoder_36_out5, decoder_36_out6,
       decoder_36_out7, decoder_37_out5, decoder_37_out6, decoder_37_out7, decoder_38_out1, decoder_38_out2,
       decoder_39_out5, decoder_39_out6, decoder_39_out7, decoder_40_out6, decoder_41_out6, decoder_42_out6,
       decoder_43_out6, decoder_44_out6, decoder_45_out6, decoder_46_out6, decoder_47_out6, nor_1_out,
       nor_2_out, not_1_out, not_2_out, not_3_out, not_4_out, not_5_out, not_7_out, not_8_out, not_9_out,
       not_10_out, not_11_out, not_12_out, not_13_out, not_14_out, not_15_out, not_16_out, not_17_out,
       not_18_out, not_19_out, not_20_out, not_21_out, not_22_out, not_23_out, not_24_out, not_25_out,
       not_26_out, not_27_out, not_28_out, not_29_out, not_30_out, not_31_out, not_32_out, not_33_out,
       not_34_out, not_35_out, not_36_out, not_37_out, not_38_out, not_39_out, not_40_out, not_41_out,
       not_42_out, not_43_out, not_44_out, not_45_out, not_46_out, not_47_out, or_1_out, or_2_out, or_3_out,
       or_4_out, or_5_out, or_6_out, or_7_out, or_8_out, or_9_out, or_10_out, or_11_out, or_12_out,
       or_13_out, or_14_out, or_15_out, or_16_out, or_17_out, or_18_out, or_19_out, or_20_out, or_21_out,
       or_22_out, or_23_out, or_24_out, or_26_out, or_27_out, or_28_out, or_29_out, or_30_out, or_31_out,
       or_32_out, or_33_out, or_34_out, or_35_out, or_36_out, or_37_out, or_38_out, or_39_out, or_40_out,
       or_41_out, or_42_out, or_43_out, or_44_out, or_45_out, or_46_out, or_47_out, pull_resistor_25_node,
       pull_resistor_26_node, pull_resistor_27_node, pull_resistor_28_node, pull_resistor_29_node,
       pull_resistor_30_node, pull_resistor_31_node, pull_resistor_32_node, pull_resistor_33_node,
       pull_resistor_34_node, pull_resistor_35_node, pull_resistor_36_node, pull_resistor_37_node,
       pull_resistor_38_node, pull_resistor_39_node, pull_resistor_41_node, pull_resistor_79_node,
       xnor_1_out, xnor_2_out, xnor_3_out, xnor_4_out, xnor_5_out, xnor_6_out, xnor_7_out, xnor_8_out,
       xnor_9_out, xnor_10_out, xnor_11_out, xnor_13_out, xnor_14_out, xnor_15_out, xor_1_out, xor_2_out,
       xor_3_out, xor_4_out, xor_9_out, xor_10_out, xor_11_out, xor_12_out, xor_13_out, xor_14_out,
       xor_15_out, xor_16_out, xor_17_out, xor_18_out, xor_19_out, xor_20_out, xor_21_out, xor_22_out,
       xor_23_out, xor_24_out, xor_42_out, xor_43_out, xor_44_out, xor_45_out, xor_46_out, xor_47_out,
       xor_48_out, xor_49_out, xor_50_out, xor_51_out, xor_52_out, xor_53_out, xor_54_out, xor_55_out,
       xor_56_out, xor_57_out;
  wire [3:0] d_ff_4_q, multiplexer_1_out, xor_8_out;
  wire [6:0] d_ff_83_q;
  wire [7:0] and_70_out, buffer_127_out, counter_1_q, d_ff_56_q, d_ff_57_q, d_ff_58_q, d_ff_59_q, d_ff_60_q,
       d_ff_61_q, d_ff_76_q, not_6_out, or_25_out, xor_41_out, xor_65_out, xor_69_out;
  wire [15:0] d_ff_20_q, multiplexer_2_out, ram_1_dout, xor_40_out;

  and and_1 (and_1_out, buffer_18_out, clock_in);
  and and_2 (and_2_out, buffer_30_out, clock_in);
  or or_1 (or_1_out, buffer_122_out, d_ff_4_q[3], or_23_out);
  or or_2 (or_2_out, and_1_out, and_2_out);
  buf and_3 (and_3_out, not_1_out);  // AND_Gate
  not not_1 (not_1_out, clock_in);
  D_Flip_Flop d_ff_1 (
    .D(multiplexer_1_out[3]), .clk(and_3_out), .Q(d_ff_4_q[3]), .reset(or_1_out));  // open: Qn, preset
  D_Flip_Flop d_ff_2 (
    .D(multiplexer_1_out[2]), .clk(and_3_out), .Q(d_ff_4_q[2]), .reset(or_1_out));  // open: Qn, preset
  D_Flip_Flop d_ff_3 (
    .D(multiplexer_1_out[1]), .clk(and_3_out), .Q(d_ff_4_q[1]), .reset(or_1_out));  // open: Qn, preset
  D_Flip_Flop d_ff_4 (
    .D(multiplexer_1_out[0]), .clk(and_3_out), .Q(d_ff_4_q[0]), .reset(or_1_out));  // open: Qn, preset
  D_Flip_Flop d_ff_5 (
    .D(multiplexer_2_out[15]), .clk(or_2_out), .Q(d_ff_20_q[15]), .reset(or_23_out));  // open: Qn, preset
  D_Flip_Flop d_ff_6 (
    .D(multiplexer_2_out[14]), .clk(or_2_out), .Q(d_ff_20_q[14]), .reset(or_23_out));  // open: Qn, preset
  D_Flip_Flop d_ff_7 (
    .D(multiplexer_2_out[13]), .clk(or_2_out), .Q(d_ff_20_q[13]), .reset(or_23_out));  // open: Qn, preset
  D_Flip_Flop d_ff_8 (
    .D(multiplexer_2_out[12]), .clk(or_2_out), .Q(d_ff_20_q[12]), .reset(or_23_out));  // open: Qn, preset
  D_Flip_Flop d_ff_9 (
    .D(multiplexer_2_out[11]), .clk(or_2_out), .Q(d_ff_20_q[11]), .reset(or_23_out));  // open: Qn, preset
  D_Flip_Flop d_ff_10 (
    .D(multiplexer_2_out[10]), .clk(or_2_out), .Q(d_ff_20_q[10]), .reset(or_23_out));  // open: Qn, preset
  D_Flip_Flop d_ff_11 (
    .D(multiplexer_2_out[9]), .clk(or_2_out), .Q(d_ff_20_q[9]), .reset(or_23_out));  // open: Qn, preset
  D_Flip_Flop d_ff_12 (
    .D(multiplexer_2_out[8]), .clk(or_2_out), .Q(d_ff_20_q[8]), .reset(or_23_out));  // open: Qn, preset
  D_Flip_Flop d_ff_13 (
    .D(multiplexer_2_out[7]), .clk(or_2_out), .Q(d_ff_20_q[7]), .reset(or_23_out));  // open: Qn, preset
  D_Flip_Flop d_ff_14 (
    .D(multiplexer_2_out[6]), .clk(or_2_out), .Q(d_ff_20_q[6]), .reset(or_23_out));  // open: Qn, preset
  D_Flip_Flop d_ff_15 (
    .D(multiplexer_2_out[5]), .clk(or_2_out), .Q(d_ff_20_q[5]), .reset(or_23_out));  // open: Qn, preset
  D_Flip_Flop d_ff_16 (
    .D(multiplexer_2_out[4]), .clk(or_2_out), .Q(d_ff_20_q[4]), .reset(or_23_out));  // open: Qn, preset
  D_Flip_Flop d_ff_17 (
    .D(multiplexer_2_out[3]), .clk(or_2_out), .Q(d_ff_20_q[3]), .reset(or_23_out));  // open: Qn, preset
  D_Flip_Flop d_ff_18 (
    .D(multiplexer_2_out[2]), .clk(or_2_out), .Q(d_ff_20_q[2]), .reset(or_23_out));  // open: Qn, preset
  D_Flip_Flop d_ff_19 (
    .D(multiplexer_2_out[1]), .clk(or_2_out), .Q(d_ff_20_q[1]), .reset(or_23_out));  // open: Qn, preset
  D_Flip_Flop d_ff_20 (
    .D(multiplexer_2_out[0]), .clk(or_2_out), .Q(d_ff_20_q[0]), .reset(or_23_out));  // open: Qn, preset
  Multiplexer #(.width(4)) multiplexer_1 (.in0(xor_8_out), .in1(4'b0000), .out(multiplexer_1_out), .sel(1'b0));
  Multiplexer #(.width(16)) multiplexer_2 (
    .in0(xor_40_out), .in1(RAM_ADDRESS), .out(multiplexer_2_out), .sel(buffer_18_out));
  xor xor_1 (xor_1_out, d_ff_4_q[3], 1'b0);
  and and_4 (and_4_out, d_ff_4_q[3], 1'b0);
  xor xor_2 (xor_2_out, d_ff_4_q[2], 1'b0);
  and and_5 (and_5_out, d_ff_4_q[2], 1'b0);
  xor xor_3 (xor_3_out, d_ff_4_q[1], 1'b0);
  and and_6 (and_6_out, d_ff_4_q[1], 1'b0);
  xor xor_4 (xor_4_out, d_ff_4_q[0], 1'b1);
  and and_7 (and_7_out, d_ff_4_q[0], 1'b1);
  and and_8 (and_8_out, xor_1_out, or_4_out);
  and and_9 (and_9_out, xor_2_out, or_5_out);
  and and_10 (and_10_out, xor_3_out, or_6_out);
  and and_11 (and_11_out, xor_4_out, 1'b0);
  xor xor_5 (xor_8_out[3], xor_1_out, or_4_out);
  or or_3 (or_3_out, and_8_out, and_4_out);
  xor xor_6 (xor_8_out[2], xor_2_out, or_5_out);
  or or_4 (or_4_out, and_9_out, and_5_out);
  xor xor_7 (xor_8_out[1], xor_3_out, or_6_out);
  or or_5 (or_5_out, and_10_out, and_6_out);
  xor xor_8 (xor_8_out[0], xor_4_out, 1'b0);
  or or_6 (or_6_out, and_11_out, and_7_out);
  xor xor_9 (xor_9_out, d_ff_20_q[15], 1'b0);
  and and_12 (and_12_out, d_ff_20_q[15], 1'b0);
  xor xor_10 (xor_10_out, d_ff_20_q[14], 1'b0);
  and and_13 (and_13_out, d_ff_20_q[14], 1'b0);
  xor xor_11 (xor_11_out, d_ff_20_q[13], 1'b0);
  and and_14 (and_14_out, d_ff_20_q[13], 1'b0);
  xor xor_12 (xor_12_out, d_ff_20_q[12], 1'b0);
  and and_15 (and_15_out, d_ff_20_q[12], 1'b0);
  xor xor_13 (xor_13_out, d_ff_20_q[11], 1'b0);
  and and_16 (and_16_out, d_ff_20_q[11], 1'b0);
  xor xor_14 (xor_14_out, d_ff_20_q[10], 1'b0);
  and and_17 (and_17_out, d_ff_20_q[10], 1'b0);
  xor xor_15 (xor_15_out, d_ff_20_q[9], 1'b0);
  and and_18 (and_18_out, d_ff_20_q[9], 1'b0);
  xor xor_16 (xor_16_out, d_ff_20_q[8], 1'b0);
  and and_19 (and_19_out, d_ff_20_q[8], 1'b0);
  xor xor_17 (xor_17_out, d_ff_20_q[7], 1'b0);
  and and_20 (and_20_out, d_ff_20_q[7], 1'b0);
  xor xor_18 (xor_18_out, d_ff_20_q[6], 1'b0);
  and and_21 (and_21_out, d_ff_20_q[6], 1'b0);
  xor xor_19 (xor_19_out, d_ff_20_q[5], 1'b0);
  and and_22 (and_22_out, d_ff_20_q[5], 1'b0);
  xor xor_20 (xor_20_out, d_ff_20_q[4], 1'b0);
  and and_23 (and_23_out, d_ff_20_q[4], 1'b0);
  xor xor_21 (xor_21_out, d_ff_20_q[3], 1'b0);
  xor xor_22 (xor_22_out, d_ff_20_q[2], 1'b0);
  xor xor_23 (xor_23_out, d_ff_20_q[1], 1'b0);
  xor xor_24 (xor_24_out, d_ff_20_q[0], 1'b1);
  and and_24 (and_24_out, xor_9_out, or_8_out);
  and and_25 (and_25_out, xor_10_out, or_9_out);
  and and_26 (and_26_out, xor_11_out, or_10_out);
  and and_27 (and_27_out, xor_12_out, or_11_out);
  and and_28 (and_28_out, xor_13_out, or_12_out);
  and and_29 (and_29_out, xor_14_out, or_13_out);
  and and_30 (and_30_out, xor_15_out, or_14_out);
  and and_31 (and_31_out, xor_16_out, or_15_out);
  and and_32 (and_32_out, xor_17_out, or_16_out);
  and and_33 (and_33_out, xor_18_out, or_17_out);
  and and_34 (and_34_out, xor_19_out, or_18_out);
  and and_35 (and_35_out, xor_20_out, or_19_out);
  and and_36 (and_36_out, d_ff_20_q[3], 1'b0);
  and and_37 (and_37_out, d_ff_20_q[2], 1'b0);
  and and_38 (and_38_out, d_ff_20_q[1], 1'b0);
  and and_39 (and_39_out, d_ff_20_q[0], 1'b1);
  xor xor_25 (xor_40_out[15], xor_9_out, or_8_out);
  or or_7 (or_7_out, and_24_out, and_12_out);
  xor xor_26 (xor_40_out[14], xor_10_out, or_9_out);
  or or_8 (or_8_out, and_25_out, and_13_out);
  xor xor_27 (xor_40_out[13], xor_11_out, or_10_out);
  or or_9 (or_9_out, and_26_out, and_14_out);
  xor xor_28 (xor_40_out[12], xor_12_out, or_11_out);
  or or_10 (or_10_out, and_27_out, and_15_out);
  xor xor_29 (xor_40_out[11], xor_13_out, or_12_out);
  or or_11 (or_11_out, and_28_out, and_16_out);
  xor xor_30 (xor_40_out[10], xor_14_out, or_13_out);
  or or_12 (or_12_out, and_29_out, and_17_out);
  xor xor_31 (xor_40_out[9], xor_15_out, or_14_out);
  or or_13 (or_13_out, and_30_out, and_18_out);
  xor xor_32 (xor_40_out[8], xor_16_out, or_15_out);
  or or_14 (or_14_out, and_31_out, and_19_out);
  xor xor_33 (xor_40_out[7], xor_17_out, or_16_out);
  or or_15 (or_15_out, and_32_out, and_20_out);
  xor xor_34 (xor_40_out[6], xor_18_out, or_17_out);
  or or_16 (or_16_out, and_33_out, and_21_out);
  xor xor_35 (xor_40_out[5], xor_19_out, or_18_out);
  or or_17 (or_17_out, and_34_out, and_22_out);
  xor xor_36 (xor_40_out[4], xor_20_out, or_19_out);
  or or_18 (or_18_out, and_35_out, and_23_out);
  xor xor_37 (xor_40_out[3], xor_21_out, or_20_out);
  and and_40 (and_40_out, xor_21_out, or_20_out);
  or or_19 (or_19_out, and_40_out, and_36_out);
  xor xor_38 (xor_40_out[2], xor_22_out, or_21_out);
  and and_41 (and_41_out, xor_22_out, or_21_out);
  or or_20 (or_20_out, and_41_out, and_37_out);
  xor xor_39 (xor_40_out[1], xor_23_out, or_22_out);
  and and_42 (and_42_out, xor_23_out, or_22_out);
  or or_21 (or_21_out, and_42_out, and_38_out);
  xor xor_40 (xor_40_out[0], xor_24_out, 1'b0);
  and and_43 (and_43_out, xor_24_out, 1'b0);
  or or_22 (or_22_out, and_43_out, and_39_out);
  assign RAM_ADDRESS = not_2_out ? d_ff_20_q : 16'bz;  // Controlled_Buffer controlled_buffer_1
  not not_2 (not_2_out, buffer_11_out);
  buf buffer_1 (buffer_1_out, decoder_22_out7);
  buf buffer_2 (buffer_2_out, decoder_22_out7);
  LED led_1 (.in(RAM_ADDRESS[15]));
  LED led_2 (.in(RAM_ADDRESS[14]));
  LED led_3 (.in(RAM_ADDRESS[13]));
  Pull_Resistor pull_resistor_1 (.node(RAM_ADDRESS[15]));
  Pull_Resistor pull_resistor_2 (.node(RAM_ADDRESS[14]));
  Pull_Resistor pull_resistor_3 (.node(RAM_ADDRESS[13]));
  buf buffer_3 (buffer_2_out, decoder_24_out7);
  buf buffer_4 (buffer_4_out, decoder_24_out7);
  buf buffer_5 (buffer_2_out, decoder_23_out7);
  buf buffer_6 (buffer_6_out, decoder_23_out7);
  LED led_4 (.in(RAM_ADDRESS[12]));
  LED led_5 (.in(RAM_ADDRESS[11]));
  LED led_6 (.in(RAM_ADDRESS[10]));
  LED led_7 (.in(RAM_ADDRESS[9]));
  Pull_Resistor pull_resistor_4 (.node(RAM_ADDRESS[12]));
  Pull_Resistor pull_resistor_5 (.node(RAM_ADDRESS[11]));
  Pull_Resistor pull_resistor_6 (.node(RAM_ADDRESS[10]));
  Pull_Resistor pull_resistor_7 (.node(RAM_ADDRESS[9]));
  buf buffer_7 (buffer_7_out, decoder_31_out2);
  LED led_8 (.in(RAM_ADDRESS[8]));
  LED led_9 (.in(RAM_ADDRESS[7]));
  LED led_10 (.in(RAM_ADDRESS[6]));
  LED led_11 (.in(RAM_ADDRESS[5]));
  Pull_Resistor pull_resistor_8 (.node(RAM_ADDRESS[8]));
  Pull_Resistor pull_resistor_9 (.node(RAM_ADDRESS[7]));
  Pull_Resistor pull_resistor_10 (.node(RAM_ADDRESS[6]));
  Pull_Resistor pull_resistor_11 (.node(RAM_ADDRESS[5]));
  buf buffer_8 (buffer_8_out, decoder_32_out6);
  buf buffer_9 (buffer_9_out, decoder_32_out6);
  buf buffer_10 (buffer_10_out, decoder_32_out6);
  buf buffer_11 (buffer_11_out, decoder_32_out6);
  LED led_12 (.in(RAM_ADDRESS[4]));
  LED led_13 (.in(RAM_ADDRESS[3]));
  LED led_14 (.in(RAM_ADDRESS[2]));
  LED led_15 (.in(RAM_ADDRESS[1]));
  Pull_Resistor pull_resistor_12 (.node(RAM_ADDRESS[4]));
  Pull_Resistor pull_resistor_13 (.node(RAM_ADDRESS[3]));
  Pull_Resistor pull_resistor_14 (.node(RAM_ADDRESS[2]));
  Pull_Resistor pull_resistor_15 (.node(RAM_ADDRESS[1]));
  buf buffer_12 (buffer_12_out, decoder_33_out6);
  buf buffer_13 (buffer_10_out, decoder_33_out6);
  buf buffer_14 (buffer_9_out, decoder_33_out6);
  buf buffer_15 (buffer_11_out, decoder_33_out6);
  LED led_16 (.in(RAM_ADDRESS[0]));
  Pull_Resistor pull_resistor_16 (.node(RAM_ADDRESS[0]));
  buf buffer_16 (buffer_11_out, decoder_34_out2);
  buf buffer_17 (buffer_17_out, decoder_34_out2);
  buf buffer_18 (buffer_18_out, decoder_34_out2);
  buf buffer_19 (buffer_19_out, decoder_25_out2);
  buf buffer_20 (buffer_2_out, decoder_25_out2);
  buf buffer_21 (buffer_9_out, decoder_22_out6);
  buf buffer_22 (buffer_22_out, decoder_22_out6);
  buf buffer_23 (buffer_10_out, decoder_22_out6);
  buf buffer_24 (buffer_11_out, decoder_22_out6);
  buf buffer_25 (buffer_25_out, decoder_38_out2);
  Button button_1 (.out(button_1_out));
  and and_44 (and_44_out, buffer_94_out, clock_in);
  and and_45 (and_45_out, buffer_97_out, clock_in);
  and and_46 (and_46_out, buffer_78_out, clock_in);
  and and_47 (and_47_out, buffer_124_out, clock_in);
  buf buffer_26 (buffer_18_out, decoder_38_out1);
  buf buffer_27 (buffer_11_out, decoder_38_out1);
  buf buffer_28 (buffer_28_out, decoder_38_out1);
  or or_23 (or_23_out, reset, button_1_out);
  D_Flip_Flop d_ff_21 (
    .D(DATA_BUS_OUTPUT[7]), .clk(and_44_out), .Q(d_ff_56_q[7]), .reset(or_23_out));  // open: Qn, preset
  D_Flip_Flop d_ff_22 (
    .D(DATA_BUS_OUTPUT[7]), .clk(and_45_out), .Q(d_ff_57_q[7]), .reset(or_23_out));  // open: Qn, preset
  D_Flip_Flop d_ff_23 (
    .D(DATA_BUS_OUTPUT[7]), .clk(and_46_out), .Q(d_ff_58_q[7]), .reset(or_23_out));  // open: Qn, preset
  and and_48 (and_48_out, buffer_74_out, clock_in);
  Counter counter_1 (
    .clr(or_23_out), .up(buffer_29_out), .count(or_24_out), .clk(clock_in), .Q(counter_1_q));  // open: load, D, carry
  or or_24 (or_24_out, buffer_29_out, buffer_25_out);
  buf buffer_29 (buffer_29_out, decoder_39_out5);
  buf buffer_30 (buffer_30_out, decoder_39_out5);
  D_Flip_Flop d_ff_24 (
    .D(DATA_BUS_OUTPUT[6]), .clk(and_44_out), .Q(d_ff_56_q[6]), .reset(or_23_out));  // open: Qn, preset
  D_Flip_Flop d_ff_25 (
    .D(DATA_BUS_OUTPUT[6]), .clk(and_46_out), .Q(d_ff_58_q[6]), .reset(or_23_out));  // open: Qn, preset
  D_Flip_Flop d_ff_26 (
    .D(DATA_BUS_OUTPUT[7]), .clk(and_48_out), .Q(d_ff_60_q[7]), .reset(or_23_out));  // open: Qn, preset
  D_Flip_Flop d_ff_27 (
    .D(DATA_BUS_OUTPUT[7]), .clk(and_47_out), .Q(d_ff_59_q[7]), .reset(or_23_out));  // open: Qn, preset
  buf buffer_31 (buffer_31_out, decoder_39_out6);
  buf buffer_32 (buffer_11_out, decoder_39_out7);
  buf buffer_33 (buffer_9_out, decoder_39_out7);
  buf buffer_34 (buffer_18_out, decoder_39_out7);
  D_Flip_Flop d_ff_28 (
    .D(DATA_BUS_OUTPUT[6]), .clk(and_45_out), .Q(d_ff_57_q[6]), .reset(or_23_out));  // open: Qn, preset
  D_Flip_Flop d_ff_29 (
    .D(DATA_BUS_OUTPUT[6]), .clk(and_48_out), .Q(d_ff_60_q[6]), .reset(or_23_out));  // open: Qn, preset
  D_Flip_Flop d_ff_30 (
    .D(DATA_BUS_OUTPUT[6]), .clk(and_47_out), .Q(d_ff_59_q[6]), .reset(or_23_out));  // open: Qn, preset
  // Buffer buffer_35 has open pins: in=decoder_39_out7, out=open
  buf buffer_36 (keyboard_load, decoder_16_out6);
  buf buffer_37 (buffer_30_out, decoder_16_out6);
  assign DATA_BUS_OUTPUT = buffer_10_out ? RAM_DATA_IN : 8'bz;  // Controlled_Buffer controlled_buffer_2
  D_Flip_Flop d_ff_31 (
    .D(DATA_BUS_OUTPUT[5]), .clk(and_44_out), .Q(d_ff_56_q[5]), .reset(or_23_out));  // open: Qn, preset
  D_Flip_Flop d_ff_32 (
    .D(DATA_BUS_OUTPUT[5]), .clk(and_45_out), .Q(d_ff_57_q[5]), .reset(or_23_out));  // open: Qn, preset
  D_Flip_Flop d_ff_33 (
    .D(DATA_BUS_OUTPUT[5]), .clk(and_46_out), .Q(d_ff_58_q[5]), .reset(or_23_out));  // open: Qn, preset
  assign RAM_ADDRESS[7:0] = buffer_17_out ? d_ff_58_q : 8'bz;  // Controlled_Buffer controlled_buffer_3
  assign RAM_ADDRESS[15:8] = buffer_17_out ? d_ff_60_q : 8'bz;  // Controlled_Buffer controlled_buffer_4
  D_Flip_Flop d_ff_34 (
    .D(DATA_BUS_OUTPUT[5]), .clk(and_47_out), .Q(d_ff_59_q[5]), .reset(or_23_out));  // open: Qn, preset
  buf buffer_38 (buffer_18_out, decoder_47_out6);
  buf buffer_39 (buffer_11_out, decoder_47_out6);
  buf buffer_40 (buffer_9_out, decoder_47_out6);
  D_Flip_Flop d_ff_35 (
    .D(DATA_BUS_OUTPUT[4]), .clk(and_44_out), .Q(d_ff_56_q[4]), .reset(or_23_out));  // open: Qn, preset
  assign RAM_ADDRESS[7:0] = buffer_9_out ? d_ff_56_q : 8'bz;  // Controlled_Buffer controlled_buffer_5
  assign RAM_ADDRESS[15:8] = buffer_9_out ? d_ff_57_q : 8'bz;  // Controlled_Buffer controlled_buffer_6
  D_Flip_Flop d_ff_36 (
    .D(DATA_BUS_OUTPUT[4]), .clk(and_46_out), .Q(d_ff_58_q[4]), .reset(or_23_out));  // open: Qn, preset
  D_Flip_Flop d_ff_37 (
    .D(DATA_BUS_OUTPUT[5]), .clk(and_48_out), .Q(d_ff_60_q[5]), .reset(or_23_out));  // open: Qn, preset
  buf buffer_41 (buffer_41_out, decoder_26_out7);
  buf buffer_42 (buffer_9_out, decoder_26_out6);
  buf buffer_43 (buffer_10_out, decoder_26_out6);
  buf buffer_44 (buffer_22_out, decoder_26_out6);
  D_Flip_Flop d_ff_38 (
    .D(DATA_BUS_OUTPUT[4]), .clk(and_45_out), .Q(d_ff_57_q[4]), .reset(or_23_out));  // open: Qn, preset
  D_Flip_Flop d_ff_39 (
    .D(DATA_BUS_OUTPUT[4]), .clk(and_48_out), .Q(d_ff_60_q[4]), .reset(or_23_out));  // open: Qn, preset
  RAM #(.dataWidth(16), .enables("line")) ram_1 (
    .addr(counter_1_q), .we(buffer_31_out), .clk(clock_in), .din(RAM_ADDRESS), .dout(ram_1_dout));
  D_Flip_Flop d_ff_40 (
    .D(DATA_BUS_OUTPUT[4]), .clk(and_47_out), .Q(d_ff_59_q[4]), .reset(or_23_out));  // open: Qn, preset
  buf buffer_45 (buffer_45_out, decoder_27_out2);
  buf buffer_46 (buffer_2_out, decoder_27_out2);
  buf buffer_47 (buffer_11_out, decoder_26_out6);
  D_Flip_Flop d_ff_41 (
    .D(DATA_BUS_OUTPUT[3]), .clk(and_44_out), .Q(d_ff_56_q[3]), .reset(or_23_out));  // open: Qn, preset
  D_Flip_Flop d_ff_42 (
    .D(DATA_BUS_OUTPUT[3]), .clk(and_45_out), .Q(d_ff_57_q[3]), .reset(or_23_out));  // open: Qn, preset
  D_Flip_Flop d_ff_43 (
    .D(DATA_BUS_OUTPUT[3]), .clk(and_46_out), .Q(d_ff_58_q[3]), .reset(or_23_out));  // open: Qn, preset
  D_Flip_Flop d_ff_44 (
    .D(DATA_BUS_OUTPUT[3]), .clk(and_47_out), .Q(d_ff_59_q[3]), .reset(or_23_out));  // open: Qn, preset
  buf buffer_48 (buffer_48_out, decoder_28_out2);
  buf buffer_49 (buffer_2_out, decoder_28_out2);
  buf buffer_50 (buffer_50_out, decoder_29_out7);
  D_Flip_Flop d_ff_45 (
    .D(DATA_BUS_OUTPUT[2]), .clk(and_44_out), .Q(d_ff_56_q[2]), .reset(or_23_out));  // open: Qn, preset
  D_Flip_Flop d_ff_46 (
    .D(DATA_BUS_OUTPUT[2]), .clk(and_45_out), .Q(d_ff_57_q[2]), .reset(or_23_out));  // open: Qn, preset
  D_Flip_Flop d_ff_47 (
    .D(DATA_BUS_OUTPUT[2]), .clk(and_46_out), .Q(d_ff_58_q[2]), .reset(or_23_out));  // open: Qn, preset
  D_Flip_Flop d_ff_48 (
    .D(DATA_BUS_OUTPUT[3]), .clk(and_48_out), .Q(d_ff_60_q[3]), .reset(or_23_out));  // open: Qn, preset
  buf buffer_51 (buffer_2_out, decoder_29_out7);
  buf buffer_52 (buffer_2_out, decoder_30_out7);
  buf buffer_53 (buffer_53_out, decoder_30_out7);
  Decoder #(.enable("false"), .select(4)) decoder_1 (
    .out0(decoder_1_out0), .out1(decoder_1_out1), .out2(decoder_1_out2), .out3(decoder_1_out3),
    .out5(decoder_1_out5), .out7(decoder_1_out7), .sel(d_ff_59_q[7:4]));  // open: out4, out6, out8, out9, out10, out11, out12, out13, out14, out15
  D_Flip_Flop d_ff_49 (
    .D(DATA_BUS_OUTPUT[1]), .clk(and_44_out), .Q(d_ff_56_q[1]), .reset(or_23_out));  // open: Qn, preset
  D_Flip_Flop d_ff_50 (
    .D(DATA_BUS_OUTPUT[1]), .clk(and_46_out), .Q(d_ff_58_q[1]), .reset(or_23_out));  // open: Qn, preset
  D_Flip_Flop d_ff_51 (
    .D(DATA_BUS_OUTPUT[2]), .clk(and_48_out), .Q(d_ff_60_q[2]), .reset(or_23_out));  // open: Qn, preset
  D_Flip_Flop d_ff_52 (
    .D(DATA_BUS_OUTPUT[2]), .clk(and_47_out), .Q(d_ff_59_q[2]), .reset(or_23_out));  // open: Qn, preset
  buf buffer_54 (buffer_54_out, decoder_15_out2);
  buf buffer_55 (RAM_WRITE, decoder_15_out2);
  D_Flip_Flop d_ff_53 (
    .D(DATA_BUS_OUTPUT[1]), .clk(and_45_out), .Q(d_ff_57_q[1]), .reset(or_23_out));  // open: Qn, preset
  D_Flip_Flop d_ff_54 (
    .D(DATA_BUS_OUTPUT[1]), .clk(and_48_out), .Q(d_ff_60_q[1]), .reset(or_23_out));  // open: Qn, preset
  D_Flip_Flop d_ff_55 (
    .D(DATA_BUS_OUTPUT[1]), .clk(and_47_out), .Q(d_ff_59_q[1]), .reset(or_23_out));  // open: Qn, preset
  buf buffer_56 (buffer_17_out, decoder_15_out2);
  buf buffer_57 (buffer_11_out, decoder_15_out2);
  D_Flip_Flop d_ff_56 (
    .D(DATA_BUS_OUTPUT[0]), .clk(and_44_out), .Q(d_ff_56_q[0]), .reset(or_23_out));  // open: Qn, preset
  D_Flip_Flop d_ff_57 (
    .D(DATA_BUS_OUTPUT[0]), .clk(and_45_out), .Q(d_ff_57_q[0]), .reset(or_23_out));  // open: Qn, preset
  D_Flip_Flop d_ff_58 (
    .D(DATA_BUS_OUTPUT[0]), .clk(and_46_out), .Q(d_ff_58_q[0]), .reset(or_23_out));  // open: Qn, preset
  assign RAM_ADDRESS = buffer_28_out ? ram_1_dout : 16'bz;  // Controlled_Buffer controlled_buffer_7
  D_Flip_Flop d_ff_59 (
    .D(DATA_BUS_OUTPUT[0]), .clk(and_47_out), .Q(d_ff_59_q[0]), .reset(or_23_out));  // open: Qn, preset
  buf buffer_58 (buffer_58_out, decoder_16_out5);
  buf buffer_59 (RAM_WRITE, decoder_16_out5);
  buf buffer_60 (buffer_9_out, decoder_16_out5);
  buf buffer_61 (buffer_11_out, decoder_16_out5);
  D_Flip_Flop d_ff_60 (
    .D(DATA_BUS_OUTPUT[0]), .clk(and_48_out), .Q(d_ff_60_q[0]), .reset(or_23_out));  // open: Qn, preset
  buf buffer_62 (buffer_9_out, decoder_17_out6);
  buf buffer_63 (buffer_63_out, decoder_17_out6);
  buf buffer_64 (RAM_WRITE, decoder_17_out6);
  buf buffer_65 (buffer_11_out, decoder_17_out6);
  buf buffer_66 (RAM_WRITE, decoder_18_out6);
  buf buffer_67 (buffer_9_out, decoder_18_out6);
  buf buffer_68 (buffer_11_out, decoder_18_out6);
  buf buffer_69 (buffer_54_out, decoder_18_out6);
  Decoder #(.select(4)) decoder_2 (
    .out0(decoder_2_out0), .out1(decoder_2_out1), .out2(decoder_2_out2), .out3(decoder_2_out3),
    .sel(d_ff_59_q[3:0]), .en(decoder_1_out2));  // open: out4, out5, out6, out7, out8, out9, out10, out11, out12, out13, out14, out15
  Decoder #(.select(4)) decoder_3 (
    .out0(decoder_3_out0), .out1(decoder_3_out1), .out2(decoder_3_out2), .sel(d_ff_59_q[3:0]),
    .en(decoder_1_out5));  // open: out3, out4, out5, out6, out7, out8, out9, out10, out11, out12, out13, out14, out15
  LED led_17 (.in(DATA_BUS_OUTPUT[7]));
  Pull_Resistor pull_resistor_17 (.node(DATA_BUS_OUTPUT[7]));
  buf buffer_70 (buffer_2_out, decoder_11_out2);
  buf buffer_71 (buffer_17_out, decoder_11_out2);
  buf buffer_72 (buffer_10_out, decoder_11_out2);
  Decoder #(.select(4)) decoder_4 (
    .out0(decoder_4_out0), .out1(decoder_4_out1), .out2(decoder_4_out2), .out3(decoder_4_out3),
    .out4(decoder_4_out4), .out5(decoder_4_out5), .out6(decoder_4_out6), .out7(decoder_4_out7),
    .out8(decoder_4_out8), .sel(d_ff_59_q[3:0]), .en(decoder_1_out3));  // open: out9, out10, out11, out12, out13, out14, out15
  LED led_18 (.in(DATA_BUS_OUTPUT[6]));
  LED led_19 (.in(DATA_BUS_OUTPUT[5]));
  LED led_20 (.in(DATA_BUS_OUTPUT[4]));
  LED led_21 (.in(DATA_BUS_OUTPUT[3]));
  Pull_Resistor pull_resistor_18 (.node(DATA_BUS_OUTPUT[6]));
  Pull_Resistor pull_resistor_19 (.node(DATA_BUS_OUTPUT[5]));
  Pull_Resistor pull_resistor_20 (.node(DATA_BUS_OUTPUT[4]));
  Pull_Resistor pull_resistor_21 (.node(DATA_BUS_OUTPUT[3]));
  buf buffer_73 (buffer_11_out, decoder_11_out2);
  Decoder #(.select(4)) decoder_5 (
    .out0(decoder_5_out0), .out1(decoder_5_out1), .out2(decoder_5_out2), .out3(decoder_5_out3),
    .out4(decoder_5_out4), .out5(decoder_5_out5), .out6(decoder_5_out6), .out7(decoder_5_out7),
    .out8(decoder_5_out8), .out9(decoder_5_out9), .out10(decoder_5_out10), .out11(decoder_5_out11),
    .out12(decoder_5_out12), .out13(decoder_5_out13), .sel(d_ff_59_q[3:0]), .en(decoder_1_out7));  // open: out14, out15
  LED led_22 (.in(DATA_BUS_OUTPUT[2]));
  LED led_23 (.in(DATA_BUS_OUTPUT[1]));
  LED led_24 (.in(DATA_BUS_OUTPUT[0]));
  Pull_Resistor pull_resistor_22 (.node(DATA_BUS_OUTPUT[2]));
  Pull_Resistor pull_resistor_23 (.node(DATA_BUS_OUTPUT[1]));
  Pull_Resistor pull_resistor_24 (.node(DATA_BUS_OUTPUT[0]));
  buf buffer_74 (buffer_74_out, decoder_12_out6);
  buf buffer_75 (buffer_9_out, decoder_12_out6);
  buf buffer_76 (buffer_10_out, decoder_12_out6);
  buf buffer_77 (buffer_11_out, decoder_12_out6);
  buf buffer_78 (buffer_78_out, decoder_13_out6);
  Decoder #(.select(4)) decoder_6 (
    .out0(decoder_6_out0), .out1(decoder_6_out1), .out2(decoder_6_out2), .out3(decoder_6_out3),
    .sel(d_ff_59_q[3:0]), .en(decoder_1_out0));  // open: out4, out5, out6, out7, out8, out9, out10, out11, out12, out13, out14, out15
  Decoder #(.select(4)) decoder_7 (
    .out0(decoder_7_out0), .out1(decoder_7_out1), .out2(decoder_7_out2), .out3(decoder_7_out3),
    .out4(decoder_7_out4), .out5(decoder_7_out5), .sel(d_ff_59_q[3:0]), .en(decoder_1_out1));  // open: out6, out7, out8, out9, out10, out11, out12, out13, out14, out15
  buf buffer_79 (buffer_9_out, decoder_13_out6);
  buf buffer_80 (buffer_10_out, decoder_13_out6);
  buf buffer_81 (buffer_11_out, decoder_13_out6);
  buf buffer_82 (tty_write, decoder_14_out6);
  buf buffer_83 (buffer_9_out, decoder_14_out6);
  buf buffer_84 (buffer_10_out, decoder_14_out6);
  buf buffer_85 (buffer_11_out, decoder_14_out6);
  assign DATA_BUS_OUTPUT[6:0] = buffer_58_out ? keyboard_data_in : 7'bz;  // Controlled_Buffer controlled_buffer_8
  buf buffer_86 (buffer_22_out, decoder_20_out6);
  Decoder #(.disabled("Z"), .select(3), .tristate("true")) decoder_8 (
    .out0(decoder_8_out0), .out1(decoder_8_out1), .out2(decoder_8_out2), .out3(decoder_8_out1),
    .out4(decoder_8_out4), .sel(d_ff_4_q[2:0]), .en(decoder_6_out3));  // open: out5, out6, out7
  Decoder #(.disabled("Z"), .select(3), .tristate("true")) decoder_9 (
    .out0(decoder_8_out0), .out1(decoder_8_out1), .out2(decoder_9_out2), .out3(decoder_8_out1),
    .out4(decoder_8_out4), .sel(d_ff_4_q[2:0]), .en(decoder_6_out2));  // open: out5, out6, out7
  Decoder #(.disabled("Z"), .select(3), .tristate("true")) decoder_10 (
    .out0(decoder_8_out0), .out1(decoder_8_out1), .out2(decoder_10_out2), .out3(decoder_8_out1),
    .out4(decoder_8_out4), .sel(d_ff_4_q[2:0]), .en(decoder_6_out1));  // open: out5, out6, out7
  Decoder #(.disabled("Z"), .select(3), .tristate("true")) decoder_11 (
    .out0(decoder_8_out0), .out1(decoder_8_out1), .out2(decoder_11_out2), .out3(decoder_8_out4),
    .sel(d_ff_4_q[2:0]), .en(decoder_7_out5));  // open: out4, out5, out6, out7
  Decoder #(.disabled("Z"), .select(3), .tristate("true")) decoder_12 (
    .out0(decoder_8_out0), .out1(decoder_8_out1), .out2(decoder_12_out2), .out3(decoder_8_out1),
    .out4(decoder_12_out4), .out5(decoder_8_out1), .out6(decoder_12_out6), .out7(decoder_8_out4),
    .sel(d_ff_4_q[2:0]), .en(decoder_7_out4));
  Decoder #(.disabled("Z"), .select(3), .tristate("true")) decoder_13 (
    .out0(decoder_8_out0), .out1(decoder_8_out1), .out2(decoder_12_out2), .out3(decoder_8_out1),
    .out4(decoder_12_out4), .out5(decoder_8_out1), .out6(decoder_13_out6), .out7(decoder_8_out4),
    .sel(d_ff_4_q[2:0]), .en(decoder_7_out3));
  Decoder #(.disabled("Z"), .select(3), .tristate("true")) decoder_14 (
    .out0(decoder_8_out0), .out1(decoder_8_out1), .out2(decoder_12_out2), .out3(decoder_8_out1),
    .out4(decoder_12_out4), .out5(decoder_8_out1), .out6(decoder_14_out6), .out7(decoder_8_out4),
    .sel(d_ff_4_q[2:0]), .en(decoder_7_out2));
  Decoder #(.disabled("Z"), .select(3), .tristate("true")) decoder_15 (
    .out0(decoder_8_out0), .out1(decoder_8_out1), .out2(decoder_15_out2), .out3(decoder_8_out4),
    .sel(d_ff_4_q[2:0]), .en(decoder_2_out3));  // open: out4, out5, out6, out7
  Decoder #(.disabled("Z"), .select(3), .tristate("true")) decoder_16 (
    .out0(decoder_8_out0), .out1(decoder_8_out1), .out2(decoder_12_out2), .out3(decoder_8_out1),
    .out4(decoder_12_out4), .out5(decoder_16_out5), .out6(decoder_16_out6), .out7(decoder_8_out4),
    .sel(d_ff_4_q[2:0]), .en(decoder_2_out2));
  Decoder #(.disabled("Z"), .select(3), .tristate("true")) decoder_17 (
    .out0(decoder_8_out0), .out1(decoder_8_out1), .out2(decoder_12_out2), .out3(decoder_8_out1),
    .out4(decoder_12_out4), .out5(decoder_8_out1), .out6(decoder_17_out6), .out7(decoder_8_out4),
    .sel(d_ff_4_q[2:0]), .en(decoder_2_out1));
  Decoder #(.disabled("Z"), .select(3), .tristate("true")) decoder_18 (
    .out0(decoder_8_out0), .out1(decoder_8_out1), .out2(decoder_12_out2), .out3(decoder_8_out1),
    .out4(decoder_12_out4), .out5(decoder_8_out1), .out6(decoder_18_out6), .out7(decoder_8_out4),
    .sel(d_ff_4_q[2:0]), .en(decoder_2_out0));
  buf buffer_87 (buffer_9_out, decoder_20_out6);
  buf buffer_88 (buffer_10_out, decoder_20_out6);
  buf buffer_89 (buffer_11_out, decoder_20_out6);
  Decoder #(.disabled("Z"), .select(3), .tristate("true")) decoder_19 (
    .out0(decoder_8_out0), .out1(decoder_8_out1), .out2(decoder_8_out4), .sel(d_ff_4_q[2:0]),
    .en(decoder_6_out0));  // open: out3, out4, out5, out6, out7
  Decoder #(.disabled("Z"), .select(3), .tristate("true")) decoder_20 (
    .out0(decoder_8_out0), .out1(decoder_8_out1), .out2(decoder_12_out2), .out3(decoder_8_out1),
    .out4(decoder_12_out4), .out5(decoder_8_out1), .out6(decoder_20_out6), .out7(decoder_8_out4),
    .sel(d_ff_4_q[2:0]), .en(decoder_7_out1));
  Decoder #(.disabled("Z"), .select(3), .tristate("true")) decoder_21 (
    .out0(decoder_8_out0), .out1(decoder_8_out1), .out2(decoder_12_out2), .out3(decoder_8_out1),
    .out4(decoder_12_out4), .out5(decoder_8_out1), .out6(decoder_21_out6), .out7(decoder_8_out4),
    .sel(d_ff_4_q[2:0]), .en(decoder_7_out0));
  Decoder #(.disabled("Z"), .select(3), .tristate("true")) decoder_22 (
    .out0(decoder_8_out0), .out1(decoder_8_out1), .out2(decoder_12_out2), .out3(decoder_8_out1),
    .out4(decoder_12_out4), .out5(decoder_8_out1), .out6(decoder_22_out6), .out7(decoder_22_out7),
    .sel(d_ff_4_q[2:0]), .en(decoder_4_out8));
  Decoder #(.disabled("Z"), .select(3), .tristate("true")) decoder_23 (
    .out0(decoder_8_out0), .out1(decoder_8_out1), .out2(decoder_12_out2), .out3(decoder_8_out1),
    .out4(decoder_12_out4), .out5(decoder_8_out1), .out6(decoder_22_out6), .out7(decoder_23_out7),
    .sel(d_ff_4_q[2:0]), .en(decoder_4_out7));
  Decoder #(.disabled("Z"), .select(3), .tristate("true")) decoder_24 (
    .out0(decoder_8_out0), .out1(decoder_8_out1), .out2(decoder_12_out2), .out3(decoder_8_out1),
    .out4(decoder_12_out4), .out5(decoder_8_out1), .out6(decoder_22_out6), .out7(decoder_24_out7),
    .sel(d_ff_4_q[2:0]), .en(decoder_4_out6));
  Decoder #(.disabled("Z"), .select(3), .tristate("true")) decoder_25 (
    .out0(decoder_8_out0), .out1(decoder_8_out1), .out2(decoder_25_out2), .out3(decoder_8_out4),
    .sel(d_ff_4_q[2:0]), .en(decoder_4_out5));  // open: out4, out5, out6, out7
  Decoder #(.disabled("Z"), .select(3), .tristate("true")) decoder_26 (
    .out0(decoder_8_out0), .out1(decoder_8_out1), .out2(decoder_12_out2), .out3(decoder_8_out1),
    .out4(decoder_12_out4), .out5(decoder_8_out1), .out6(decoder_26_out6), .out7(decoder_26_out7),
    .sel(d_ff_4_q[2:0]), .en(decoder_4_out4));
  Decoder #(.disabled("Z"), .select(3), .tristate("true")) decoder_27 (
    .out0(decoder_8_out0), .out1(decoder_8_out1), .out2(decoder_27_out2), .out3(decoder_8_out4),
    .sel(d_ff_4_q[2:0]), .en(decoder_4_out3));  // open: out4, out5, out6, out7
  Decoder #(.disabled("Z"), .select(3), .tristate("true")) decoder_28 (
    .out0(decoder_8_out0), .out1(decoder_8_out1), .out2(decoder_28_out2), .out3(decoder_8_out4),
    .sel(d_ff_4_q[2:0]), .en(decoder_4_out2));  // open: out4, out5, out6, out7
  Decoder #(.disabled("Z"), .select(3), .tristate("true")) decoder_29 (
    .out0(decoder_8_out0), .out1(decoder_8_out1), .out2(decoder_12_out2), .out3(decoder_8_out1),
    .out4(decoder_12_out4), .out5(decoder_8_out1), .out6(decoder_22_out6), .out7(decoder_29_out7),
    .sel(d_ff_4_q[2:0]), .en(decoder_4_out1));
  Decoder #(.disabled("Z"), .select(3), .tristate("true")) decoder_30 (
    .out0(decoder_8_out0), .out1(decoder_8_out1), .out2(decoder_12_out2), .out3(decoder_8_out1),
    .out4(decoder_12_out4), .out5(decoder_8_out1), .out6(decoder_22_out6), .out7(decoder_30_out7),
    .sel(d_ff_4_q[2:0]), .en(decoder_4_out0));
  Decoder #(.disabled("Z"), .select(3), .tristate("true")) decoder_31 (
    .out0(decoder_8_out0), .out1(decoder_8_out1), .out2(decoder_31_out2), .out3(decoder_8_out4),
    .sel(d_ff_4_q[2:0]), .en(decoder_3_out2));  // open: out4, out5, out6, out7
  Decoder #(.disabled("Z"), .select(3), .tristate("true")) decoder_32 (
    .out0(decoder_8_out0), .out1(decoder_8_out1), .out2(decoder_12_out2), .out3(decoder_8_out1),
    .out4(decoder_12_out4), .out5(decoder_8_out1), .out6(decoder_32_out6), .out7(decoder_8_out4),
    .sel(d_ff_4_q[2:0]), .en(decoder_3_out1));
  Decoder #(.disabled("Z"), .select(3), .tristate("true")) decoder_33 (
    .out0(decoder_8_out0), .out1(decoder_8_out1), .out2(decoder_12_out2), .out3(decoder_8_out1),
    .out4(decoder_12_out4), .out5(decoder_8_out1), .out6(decoder_33_out6), .out7(decoder_8_out4),
    .sel(d_ff_4_q[2:0]), .en(decoder_3_out0));
  and and_49 (and_49_out, buffer_2_out, clock_in);
  and and_50 (and_50_out, buffer_22_out, clock_in);
  buf buffer_90 (buffer_2_out, decoder_21_out6);
  D_Flip_Flop d_ff_61 (
    .D(DATA_BUS_OUTPUT[7]), .clk(and_49_out), .Q(d_ff_61_q[7]), .reset(or_23_out));  // open: Qn, preset
  D_Flip_Flop d_ff_62 (
    .D(DATA_BUS_OUTPUT[7]), .clk(and_50_out), .Q(d_ff_76_q[7]), .reset(or_23_out));  // open: Qn, preset
  buf buffer_91 (buffer_9_out, decoder_21_out6);
  buf buffer_92 (buffer_10_out, decoder_21_out6);
  buf buffer_93 (buffer_11_out, decoder_21_out6);
  Decoder #(.disabled("Z"), .select(3), .tristate("true")) decoder_34 (
    .out0(decoder_8_out0), .out1(decoder_8_out1), .out2(decoder_34_out2), .out3(decoder_8_out4),
    .sel(d_ff_4_q[2:0]), .en(decoder_5_out13));  // open: out4, out5, out6, out7
  Decoder #(.disabled("Z"), .select(3), .tristate("true")) decoder_35 (
    .out0(decoder_8_out0), .out1(decoder_8_out1), .out2(decoder_12_out2), .out3(decoder_8_out1),
    .out4(decoder_12_out4), .out5(decoder_35_out5), .out6(decoder_35_out6), .out7(decoder_35_out7),
    .sel(d_ff_4_q[2:0]), .en(decoder_5_out12));
  Decoder #(.disabled("Z"), .select(3), .tristate("true")) decoder_36 (
    .out0(decoder_8_out0), .out1(decoder_8_out1), .out2(decoder_12_out2), .out3(decoder_8_out1),
    .out4(decoder_12_out4), .out5(decoder_36_out5), .out6(decoder_36_out6), .out7(decoder_36_out7),
    .sel(d_ff_4_q[2:0]), .en(decoder_5_out11));
  Decoder #(.disabled("Z"), .select(3), .tristate("true")) decoder_37 (
    .out0(decoder_8_out0), .out1(decoder_8_out1), .out2(decoder_12_out2), .out3(decoder_8_out1),
    .out4(decoder_12_out4), .out5(decoder_37_out5), .out6(decoder_37_out6), .out7(decoder_37_out7),
    .sel(d_ff_4_q[2:0]), .en(decoder_5_out10));
  Decoder #(.disabled("Z"), .select(3), .tristate("true")) decoder_38 (
    .out0(decoder_8_out0), .out1(decoder_38_out1), .out2(decoder_38_out2), .out3(decoder_8_out4),
    .sel(d_ff_4_q[2:0]), .en(decoder_5_out9));  // open: out4, out5, out6, out7
  Decoder #(.disabled("Z"), .select(3), .tristate("true")) decoder_39 (
    .out0(decoder_8_out0), .out1(decoder_8_out1), .out2(decoder_12_out2), .out3(decoder_8_out1),
    .out4(decoder_12_out4), .out5(decoder_39_out5), .out6(decoder_39_out6), .out7(decoder_39_out7),
    .sel(d_ff_4_q[2:0]), .en(decoder_5_out8));
  Decoder #(.disabled("Z"), .select(3), .tristate("true")) decoder_40 (
    .out0(decoder_8_out0), .out1(decoder_8_out1), .out2(decoder_12_out2), .out3(decoder_8_out1),
    .out4(decoder_12_out4), .out5(decoder_8_out1), .out6(decoder_40_out6), .out7(decoder_8_out4),
    .sel(d_ff_4_q[2:0]), .en(decoder_5_out7));
  Decoder #(.disabled("Z"), .select(3), .tristate("true")) decoder_41 (
    .out0(decoder_8_out0), .out1(decoder_8_out1), .out2(decoder_12_out2), .out3(decoder_8_out1),
    .out4(decoder_12_out4), .out5(decoder_8_out1), .out6(decoder_41_out6), .out7(decoder_8_out4),
    .sel(d_ff_4_q[2:0]), .en(decoder_5_out6));
  Decoder #(.disabled("Z"), .select(3), .tristate("true")) decoder_42 (
    .out0(decoder_8_out0), .out1(decoder_8_out1), .out2(decoder_12_out2), .out3(decoder_8_out1),
    .out4(decoder_12_out4), .out5(decoder_8_out1), .out6(decoder_42_out6), .out7(decoder_8_out4),
    .sel(d_ff_4_q[2:0]), .en(decoder_5_out5));
  Decoder #(.disabled("Z"), .select(3), .tristate("true")) decoder_43 (
    .out0(decoder_8_out0), .out1(decoder_8_out1), .out2(decoder_12_out2), .out3(decoder_8_out1),
    .out4(decoder_12_out4), .out5(decoder_8_out1), .out6(decoder_43_out6), .out7(decoder_8_out4),
    .sel(d_ff_4_q[2:0]), .en(decoder_5_out4));
  Decoder #(.disabled("Z"), .select(3), .tristate("true")) decoder_44 (
    .out0(decoder_8_out0), .out1(decoder_8_out1), .out2(decoder_12_out2), .out3(decoder_8_out1),
    .out4(decoder_12_out4), .out5(decoder_8_out1), .out6(decoder_44_out6), .out7(decoder_8_out4),
    .sel(d_ff_4_q[2:0]), .en(decoder_5_out3));
  Decoder #(.disabled("Z"), .select(3), .tristate("true")) decoder_45 (
    .out0(decoder_8_out0), .out1(decoder_8_out1), .out2(decoder_12_out2), .out3(decoder_8_out1),
    .out4(decoder_12_out4), .out5(decoder_8_out1), .out6(decoder_45_out6), .out7(decoder_8_out4),
    .sel(d_ff_4_q[2:0]), .en(decoder_5_out2));
  Decoder #(.disabled("Z"), .select(3), .tristate("true")) decoder_46 (
    .out0(decoder_8_out0), .out1(decoder_8_out1), .out2(decoder_12_out2), .out3(decoder_8_out1),
    .out4(decoder_12_out4), .out5(decoder_8_out1), .out6(decoder_46_out6), .out7(decoder_8_out4),
    .sel(d_ff_4_q[2:0]), .en(decoder_5_out1));
  Decoder #(.disabled("Z"), .select(3), .tristate("true")) decoder_47 (
    .out0(decoder_8_out0), .out1(decoder_8_out1), .out2(decoder_12_out2), .out3(decoder_8_out1),
    .out4(decoder_12_out4), .out5(decoder_8_out1), .out6(decoder_47_out6), .out7(decoder_8_out4),
    .sel(d_ff_4_q[2:0]), .en(decoder_5_out0));
  D_Flip_Flop d_ff_63 (
    .D(DATA_BUS_OUTPUT[6]), .clk(and_49_out), .Q(d_ff_61_q[6]), .reset(or_23_out));  // open: Qn, preset
  D_Flip_Flop d_ff_64 (
    .D(DATA_BUS_OUTPUT[6]), .clk(and_50_out), .Q(d_ff_76_q[6]), .reset(or_23_out));  // open: Qn, preset
  buf buffer_94 (buffer_94_out, decoder_12_out4);
  buf buffer_95 (buffer_10_out, decoder_12_out4);
  buf buffer_96 (buffer_10_out, decoder_12_out2);
  buf buffer_97 (buffer_97_out, decoder_12_out2);
  D_Flip_Flop d_ff_65 (
    .D(DATA_BUS_OUTPUT[5]), .clk(and_49_out), .Q(d_ff_61_q[5]), .reset(or_23_out));  // open: Qn, preset
  assign DATA_BUS_OUTPUT = buffer_54_out ? d_ff_61_q : 8'bz;  // Controlled_Buffer controlled_buffer_9
  D_Flip_Flop d_ff_66 (
    .D(DATA_BUS_OUTPUT[5]), .clk(and_50_out), .Q(d_ff_76_q[5]), .reset(or_23_out));  // open: Qn, preset
  assign DATA_BUS_OUTPUT = buffer_63_out ? d_ff_76_q : 8'bz;  // Controlled_Buffer controlled_buffer_10
  D_Flip_Flop d_ff_67 (
    .D(DATA_BUS_OUTPUT[4]), .clk(and_49_out), .Q(d_ff_61_q[4]), .reset(or_23_out));  // open: Qn, preset
  D_Flip_Flop d_ff_68 (
    .D(DATA_BUS_OUTPUT[4]), .clk(and_50_out), .Q(d_ff_76_q[4]), .reset(or_23_out));  // open: Qn, preset
  buf buffer_98 (tty_write, decoder_8_out2);
  buf buffer_99 (buffer_10_out, decoder_8_out2);
  Pull_Resistor pull_resistor_25 (.node(pull_resistor_25_node));
  buf buffer_100 (pull_resistor_25_node, decoder_36_out7);
  Pull_Resistor pull_resistor_26 (.node(pull_resistor_26_node));
  buf buffer_101 (pull_resistor_26_node, decoder_37_out5);
  not not_3 (not_3_out, d_ff_83_q[6]);
  Pull_Resistor pull_resistor_27 (.node(pull_resistor_27_node));
  buf buffer_102 (pull_resistor_27_node, decoder_37_out5);
  buf buffer_103 (buffer_103_out, decoder_37_out6);
  buf buffer_104 (buffer_104_out, decoder_40_out6);
  Pull_Resistor pull_resistor_28 (.node(pull_resistor_28_node));
  buf buffer_105 (pull_resistor_28_node, decoder_41_out6);
  Pull_Resistor pull_resistor_29 (.node(pull_resistor_29_node));
  buf buffer_106 (pull_resistor_29_node, decoder_42_out6);
  Pull_Resistor pull_resistor_30 (.node(pull_resistor_30_node));
  buf buffer_107 (pull_resistor_30_node, decoder_43_out6);
  Pull_Resistor pull_resistor_31 (.node(pull_resistor_31_node));
  buf buffer_108 (pull_resistor_31_node, decoder_44_out6);
  Pull_Resistor pull_resistor_32 (.node(pull_resistor_32_node));
  buf buffer_109 (pull_resistor_32_node, decoder_45_out6);
  Pull_Resistor pull_resistor_33 (.node(pull_resistor_33_node));
  buf buffer_110 (pull_resistor_33_node, decoder_46_out6);
  buf buffer_111 (buffer_10_out, decoder_10_out2);
  buf buffer_112 (buffer_2_out, decoder_10_out2);
  buf buffer_113 (buffer_22_out, decoder_9_out2);
  buf buffer_114 (buffer_10_out, decoder_9_out2);
  Pull_Resistor pull_resistor_34 (.node(pull_resistor_34_node));
  buf buffer_115 (pull_resistor_34_node, decoder_35_out5);
  not not_4 (not_4_out, d_ff_83_q[4]);
  Pull_Resistor pull_resistor_35 (.node(pull_resistor_35_node));
  buf buffer_116 (pull_resistor_35_node, decoder_35_out5);
  and and_51 (and_51_out, pull_resistor_35_node, d_ff_83_q[4]);
  Pull_Resistor pull_resistor_36 (.node(pull_resistor_36_node));
  buf buffer_117 (pull_resistor_36_node, decoder_35_out6);
  and and_52 (and_52_out, pull_resistor_36_node, d_ff_83_q[4]);
  Pull_Resistor pull_resistor_37 (.node(pull_resistor_37_node));
  buf buffer_118 (pull_resistor_37_node, decoder_35_out7);
  and and_53 (and_53_out, pull_resistor_37_node, d_ff_83_q[4]);
  Pull_Resistor pull_resistor_38 (.node(pull_resistor_38_node));
  buf buffer_119 (pull_resistor_38_node, decoder_36_out5);
  and and_54 (and_54_out, pull_resistor_38_node, d_ff_83_q[5]);
  Pull_Resistor pull_resistor_39 (.node(pull_resistor_39_node));
  buf buffer_120 (pull_resistor_39_node, decoder_36_out6);
  and and_55 (and_55_out, pull_resistor_25_node, d_ff_83_q[5]);
  and and_56 (and_56_out, pull_resistor_26_node, not_3_out);
  assign decoder_8_out1 = and_56_out ? and_56_out : 1'bz;  // Controlled_Buffer controlled_buffer_11
  and and_57 (and_57_out, pull_resistor_27_node, d_ff_83_q[6]);
  Pull_Resistor pull_resistor_40 (.node(buffer_103_out));
  and and_58 (and_58_out, buffer_103_out, d_ff_83_q[6]);
  Pull_Resistor pull_resistor_41 (.node(pull_resistor_41_node));
  buf buffer_121 (pull_resistor_41_node, decoder_37_out7);
  and and_59 (and_59_out, pull_resistor_41_node, d_ff_83_q[6]);
  Pull_Resistor pull_resistor_42 (.node(buffer_104_out));
  and and_60 (and_60_out, buffer_104_out, d_ff_83_q[6]);
  and and_61 (and_61_out, pull_resistor_28_node, d_ff_83_q[5]);
  assign decoder_47_out6 = and_61_out ? and_61_out : 1'bz;  // Controlled_Buffer controlled_buffer_12
  and and_62 (and_62_out, pull_resistor_29_node, d_ff_83_q[4]);
  assign decoder_47_out6 = and_62_out ? and_62_out : 1'bz;  // Controlled_Buffer controlled_buffer_13
  and and_63 (and_63_out, pull_resistor_30_node, d_ff_83_q[3]);
  assign decoder_47_out6 = and_63_out ? and_63_out : 1'bz;  // Controlled_Buffer controlled_buffer_14
  and and_64 (and_64_out, pull_resistor_31_node, d_ff_83_q[2]);
  and and_65 (and_65_out, pull_resistor_32_node, d_ff_83_q[1]);
  and and_66 (and_66_out, pull_resistor_33_node, d_ff_83_q[0]);
  D_Flip_Flop d_ff_69 (
    .D(DATA_BUS_OUTPUT[3]), .clk(and_49_out), .Q(d_ff_61_q[3]), .reset(or_23_out));  // open: Qn, preset
  D_Flip_Flop d_ff_70 (
    .D(DATA_BUS_OUTPUT[3]), .clk(and_50_out), .Q(d_ff_76_q[3]), .reset(or_23_out));  // open: Qn, preset
  buf buffer_122 (buffer_122_out, decoder_8_out4);
  buf buffer_123 (buffer_30_out, decoder_8_out1);
  buf buffer_124 (buffer_124_out, decoder_8_out0);
  buf buffer_125 (buffer_10_out, decoder_8_out0);
  and and_67 (and_67_out, pull_resistor_34_node, not_4_out);
  assign decoder_39_out5 = and_51_out ? and_51_out : 1'bz;  // Controlled_Buffer controlled_buffer_15
  assign decoder_39_out6 = and_52_out ? and_52_out : 1'bz;  // Controlled_Buffer controlled_buffer_16
  assign decoder_39_out7 = and_53_out ? and_53_out : 1'bz;  // Controlled_Buffer controlled_buffer_17
  assign decoder_39_out5 = and_54_out ? and_54_out : 1'bz;  // Controlled_Buffer controlled_buffer_18
  and and_68 (and_68_out, pull_resistor_39_node, d_ff_83_q[5]);
  assign decoder_8_out1 = and_68_out ? and_68_out : 1'bz;  // Controlled_Buffer controlled_buffer_19
  assign decoder_39_out7 = and_55_out ? and_55_out : 1'bz;  // Controlled_Buffer controlled_buffer_20
  assign decoder_39_out5 = and_57_out ? and_57_out : 1'bz;  // Controlled_Buffer controlled_buffer_21
  assign decoder_39_out6 = and_58_out ? and_58_out : 1'bz;  // Controlled_Buffer controlled_buffer_22
  assign decoder_39_out7 = and_59_out ? and_59_out : 1'bz;  // Controlled_Buffer controlled_buffer_23
  assign decoder_47_out6 = and_60_out ? and_60_out : 1'bz;  // Controlled_Buffer controlled_buffer_24
  assign decoder_47_out6 = and_64_out ? and_64_out : 1'bz;  // Controlled_Buffer controlled_buffer_25
  assign decoder_47_out6 = and_65_out ? and_65_out : 1'bz;  // Controlled_Buffer controlled_buffer_26
  assign decoder_47_out6 = and_66_out ? and_66_out : 1'bz;  // Controlled_Buffer controlled_buffer_27
  D_Flip_Flop d_ff_71 (
    .D(DATA_BUS_OUTPUT[2]), .clk(and_49_out), .Q(d_ff_61_q[2]), .reset(or_23_out));  // open: Qn, preset
  D_Flip_Flop d_ff_72 (
    .D(DATA_BUS_OUTPUT[2]), .clk(and_50_out), .Q(d_ff_76_q[2]), .reset(or_23_out));  // open: Qn, preset
  Pull_Resistor pull_resistor_43 (.node(buffer_1_out));
  Pull_Resistor pull_resistor_44 (.node(buffer_6_out));
  Pull_Resistor pull_resistor_45 (.node(buffer_4_out));
  Pull_Resistor pull_resistor_46 (.node(buffer_19_out));
  Pull_Resistor pull_resistor_47 (.node(buffer_7_out));
  Pull_Resistor pull_resistor_48 (.node(buffer_8_out));
  Pull_Resistor pull_resistor_49 (.node(buffer_12_out));
  Pull_Resistor pull_resistor_50 (.node(buffer_25_out));
  Pull_Resistor pull_resistor_51 (.node(buffer_28_out));
  Pull_Resistor pull_resistor_52 (.node(buffer_31_out));
  Pull_Resistor pull_resistor_53 (.node(buffer_29_out));
  Pull_Resistor pull_resistor_54 (.node(buffer_17_out));
  Pull_Resistor pull_resistor_55 (.node(buffer_74_out));
  Pull_Resistor pull_resistor_56 (.node(buffer_78_out));
  Pull_Resistor pull_resistor_57 (.node(buffer_41_out));
  Pull_Resistor pull_resistor_58 (.node(buffer_18_out));
  Pull_Resistor pull_resistor_59 (.node(buffer_45_out));
  Pull_Resistor pull_resistor_60 (.node(buffer_48_out));
  Pull_Resistor pull_resistor_61 (.node(buffer_50_out));
  Pull_Resistor pull_resistor_62 (.node(buffer_53_out));
  Pull_Resistor pull_resistor_63 (.node(keyboard_load));
  Pull_Resistor pull_resistor_64 (.node(buffer_58_out));
  Pull_Resistor pull_resistor_65 (.node(buffer_63_out));
  Pull_Resistor pull_resistor_66 (.node(RAM_WRITE));
  Pull_Resistor pull_resistor_67 (.node(buffer_54_out));
  Pull_Resistor pull_resistor_68 (.node(buffer_9_out));
  Pull_Resistor pull_resistor_69 (.node(buffer_94_out));
  Pull_Resistor pull_resistor_70 (.node(buffer_97_out));
  Pull_Resistor pull_resistor_71 (.node(tty_write));
  Pull_Resistor pull_resistor_72 (.node(buffer_22_out));
  Pull_Resistor pull_resistor_73 (.node(buffer_2_out));
  Pull_Resistor pull_resistor_74 (.node(buffer_122_out));
  Pull_Resistor pull_resistor_75 (.node(buffer_30_out));
  Pull_Resistor pull_resistor_76 (.node(buffer_124_out));
  Pull_Resistor pull_resistor_77 (.node(buffer_10_out));
  Pull_Resistor pull_resistor_78 (.node(buffer_11_out));
  assign decoder_8_out1 = and_67_out ? and_67_out : 1'bz;  // Controlled_Buffer controlled_buffer_28
  D_Flip_Flop d_ff_73 (
    .D(DATA_BUS_OUTPUT[1]), .clk(and_49_out), .Q(d_ff_61_q[1]), .reset(or_23_out));  // open: Qn, preset
  D_Flip_Flop d_ff_74 (
    .D(DATA_BUS_OUTPUT[1]), .clk(and_50_out), .Q(d_ff_76_q[1]), .reset(or_23_out));  // open: Qn, preset
  D_Flip_Flop d_ff_75 (
    .D(DATA_BUS_OUTPUT[0]), .clk(and_49_out), .Q(d_ff_61_q[0]), .reset(or_23_out));  // open: Qn, preset
  D_Flip_Flop d_ff_76 (
    .D(DATA_BUS_OUTPUT[0]), .clk(and_50_out), .Q(d_ff_76_q[0]), .reset(or_23_out));  // open: Qn, preset
  Pull_Resistor pull_resistor_79 (.node(pull_resistor_79_node));
  buf buffer_126 (pull_resistor_79_node, decoder_36_out5);
  not not_5 (not_5_out, d_ff_83_q[5]);
  and and_69 (and_69_out, pull_resistor_79_node, not_5_out);
  assign decoder_8_out1 = and_69_out ? and_69_out : 1'bz;  // Controlled_Buffer controlled_buffer_29
  assign not_6_out = ~d_ff_61_q;  // NOT_Gate not_6, 8 bits wide
  assign and_70_out = d_ff_61_q & d_ff_76_q;  // AND_Gate and_70, 8 bits wide
  assign or_25_out = d_ff_61_q | d_ff_76_q;  // OR_Gate or_25, 8 bits wide
  assign xor_41_out = d_ff_61_q ^ d_ff_76_q;  // XOR_Gate xor_41, 8 bits wide
  assign DATA_BUS_OUTPUT = buffer_19_out ? not_6_out : 8'bz;  // Controlled_Buffer controlled_buffer_30
  assign DATA_BUS_OUTPUT = buffer_4_out ? and_70_out : 8'bz;  // Controlled_Buffer controlled_buffer_31
  assign DATA_BUS_OUTPUT = buffer_6_out ? or_25_out : 8'bz;  // Controlled_Buffer controlled_buffer_32
  assign DATA_BUS_OUTPUT = buffer_1_out ? xor_41_out : 8'bz;  // Controlled_Buffer controlled_buffer_33
  not not_7 (not_7_out, d_ff_61_q[3]);
  not not_8 (not_8_out, d_ff_61_q[2]);
  not not_9 (not_9_out, d_ff_61_q[1]);
  not not_10 (not_10_out, d_ff_61_q[0]);
  not not_11 (not_11_out, d_ff_61_q[7]);
  not not_12 (not_12_out, d_ff_76_q[7]);
  not not_13 (not_13_out, d_ff_61_q[6]);
  not not_14 (not_14_out, d_ff_76_q[6]);
  not not_15 (not_15_out, d_ff_61_q[5]);
  not not_16 (not_16_out, d_ff_76_q[5]);
  not not_17 (not_17_out, d_ff_61_q[4]);
  not not_18 (not_18_out, d_ff_76_q[4]);
  xor xor_42 (xor_42_out, d_ff_61_q[7], d_ff_76_q[7]);
  and and_71 (and_71_out, d_ff_61_q[7], d_ff_76_q[7]);
  xor xor_43 (xor_43_out, d_ff_61_q[6], d_ff_76_q[6]);
  and and_72 (and_72_out, d_ff_61_q[6], d_ff_76_q[6]);
  xor xor_44 (xor_44_out, d_ff_61_q[5], d_ff_76_q[5]);
  and and_73 (and_73_out, d_ff_61_q[5], d_ff_76_q[5]);
  xor xor_45 (xor_45_out, d_ff_61_q[4], d_ff_76_q[4]);
  and and_74 (and_74_out, d_ff_61_q[4], d_ff_76_q[4]);
  xor xor_46 (xor_46_out, d_ff_61_q[3], d_ff_76_q[3]);
  and and_75 (and_75_out, d_ff_61_q[3], d_ff_76_q[3]);
  xor xor_47 (xor_47_out, d_ff_61_q[2], d_ff_76_q[2]);
  and and_76 (and_76_out, d_ff_61_q[2], d_ff_76_q[2]);
  xor xor_48 (xor_48_out, d_ff_61_q[1], d_ff_76_q[1]);
  and and_77 (and_77_out, d_ff_61_q[1], d_ff_76_q[1]);
  xor xor_49 (xor_49_out, d_ff_61_q[0], d_ff_76_q[0]);
  and and_78 (and_78_out, d_ff_61_q[0], d_ff_76_q[0]);
  not not_19 (not_19_out, d_ff_61_q[7]);
  not not_20 (not_20_out, d_ff_61_q[6]);
  not not_21 (not_21_out, d_ff_61_q[5]);
  not not_22 (not_22_out, d_ff_61_q[4]);
  xor xor_50 (xor_50_out, d_ff_61_q[3], d_ff_76_q[3]);
  and and_79 (and_79_out, not_7_out, d_ff_76_q[3]);
  xor xor_51 (xor_51_out, d_ff_61_q[2], d_ff_76_q[2]);
  and and_80 (and_80_out, not_8_out, d_ff_76_q[2]);
  xor xor_52 (xor_52_out, d_ff_61_q[1], d_ff_76_q[1]);
  and and_81 (and_81_out, not_9_out, d_ff_76_q[1]);
  xor xor_53 (xor_53_out, d_ff_61_q[0], d_ff_76_q[0]);
  and and_82 (and_82_out, not_10_out, d_ff_76_q[0]);
  and and_83 (and_83_out, d_ff_61_q[7], not_12_out);
  and and_84 (and_84_out, not_11_out, d_ff_76_q[7]);
  and and_85 (and_85_out, d_ff_61_q[6], not_14_out);
  and and_86 (and_86_out, not_13_out, d_ff_76_q[6]);
  and and_87 (and_87_out, d_ff_61_q[5], not_16_out);
  and and_88 (and_88_out, not_15_out, d_ff_76_q[5]);
  and and_89 (and_89_out, d_ff_61_q[4], not_18_out);
  and and_90 (and_90_out, not_17_out, d_ff_76_q[4]);
  xnor xnor_1 (xnor_1_out, d_ff_61_q[7], d_ff_76_q[7]);
  xnor xnor_2 (xnor_2_out, d_ff_61_q[6], d_ff_76_q[6]);
  xnor xnor_3 (xnor_3_out, d_ff_61_q[5], d_ff_76_q[5]);
  xnor xnor_4 (xnor_4_out, d_ff_61_q[4], d_ff_76_q[4]);
  and and_91 (and_91_out, d_ff_61_q[3], not_24_out);
  not not_23 (not_23_out, d_ff_61_q[3]);
  not not_24 (not_24_out, d_ff_76_q[3]);
  and and_92 (and_92_out, not_23_out, d_ff_76_q[3]);
  and and_93 (and_93_out, d_ff_61_q[2], not_26_out);
  not not_25 (not_25_out, d_ff_61_q[2]);
  not not_26 (not_26_out, d_ff_76_q[2]);
  and and_94 (and_94_out, not_25_out, d_ff_76_q[2]);
  and and_95 (and_95_out, d_ff_61_q[1], not_28_out);
  not not_27 (not_27_out, d_ff_61_q[1]);
  not not_28 (not_28_out, d_ff_76_q[1]);
  and and_96 (and_96_out, not_27_out, d_ff_76_q[1]);
  and and_97 (and_97_out, d_ff_61_q[0], not_30_out);
  not not_29 (not_29_out, d_ff_61_q[0]);
  not not_30 (not_30_out, d_ff_76_q[0]);
  and and_98 (and_98_out, not_29_out, d_ff_76_q[0]);
  xnor xnor_5 (xnor_5_out, d_ff_61_q[3], d_ff_76_q[3]);
  xnor xnor_6 (xnor_6_out, d_ff_61_q[2], d_ff_76_q[2]);
  xnor xnor_7 (xnor_7_out, d_ff_61_q[1], d_ff_76_q[1]);
  xnor xnor_8 (xnor_8_out, d_ff_61_q[0], d_ff_76_q[0]);
  and and_99 (and_99_out, xor_42_out, or_27_out);
  and and_100 (and_100_out, xor_43_out, or_28_out);
  and and_101 (and_101_out, xor_44_out, or_29_out);
  and and_102 (and_102_out, xor_45_out, or_30_out);
  and and_103 (and_103_out, xor_46_out, or_31_out);
  and and_104 (and_104_out, xor_47_out, or_32_out);
  and and_105 (and_105_out, xor_48_out, or_33_out);
  and and_106 (and_106_out, xor_49_out, 1'b0);
  xor xor_54 (xor_54_out, d_ff_61_q[7], d_ff_76_q[7]);
  and and_107 (and_107_out, not_19_out, d_ff_76_q[7]);
  xor xor_55 (xor_55_out, d_ff_61_q[6], d_ff_76_q[6]);
  and and_108 (and_108_out, not_20_out, d_ff_76_q[6]);
  xor xor_56 (xor_56_out, d_ff_61_q[5], d_ff_76_q[5]);
  and and_109 (and_109_out, not_21_out, d_ff_76_q[5]);
  xor xor_57 (xor_57_out, d_ff_61_q[4], d_ff_76_q[4]);
  and and_110 (and_110_out, not_22_out, d_ff_76_q[4]);
  not not_31 (not_31_out, xor_50_out);
  not not_32 (not_32_out, xor_51_out);
  not not_33 (not_33_out, xor_52_out);
  not not_34 (not_34_out, xor_53_out);
  xnor xnor_9 (xnor_9_out, and_83_out, and_84_out);
  xnor xnor_10 (xnor_10_out, and_85_out, and_86_out);
  xnor xnor_11 (xnor_11_out, and_87_out, and_88_out);
  // XNOR_Gate xnor_12 has open pins: in0=and_89_out, in1=and_90_out, out=open
  and and_111 (and_111_out, xnor_1_out, xnor_2_out, xnor_3_out, xnor_4_out);
  xnor xnor_13 (xnor_13_out, and_91_out, and_92_out);
  xnor xnor_14 (xnor_14_out, and_93_out, and_94_out);
  xnor xnor_15 (xnor_15_out, and_95_out, and_96_out);
  // XNOR_Gate xnor_16 has open pins: in0=and_97_out, in1=and_98_out, out=open
  and and_112 (and_112_out, xnor_5_out, xnor_6_out, xnor_7_out, xnor_8_out);
  xor xor_58 (xor_65_out[7], xor_42_out, or_27_out);
  or or_26 (or_26_out, and_99_out, and_71_out);
  xor xor_59 (xor_65_out[6], xor_43_out, or_28_out);
  or or_27 (or_27_out, and_100_out, and_72_out);
  xor xor_60 (xor_65_out[5], xor_44_out, or_29_out);
  or or_28 (or_28_out, and_101_out, and_73_out);
  xor xor_61 (xor_65_out[4], xor_45_out, or_30_out);
  or or_29 (or_29_out, and_102_out, and_74_out);
  xor xor_62 (xor_65_out[3], xor_46_out, or_31_out);
  or or_30 (or_30_out, and_103_out, and_75_out);
  xor xor_63 (xor_65_out[2], xor_47_out, or_32_out);
  or or_31 (or_31_out, and_104_out, and_76_out);
  xor xor_64 (xor_65_out[1], xor_48_out, or_33_out);
  or or_32 (or_32_out, and_105_out, and_77_out);
  xor xor_65 (xor_65_out[0], xor_49_out, 1'b0);
  or or_33 (or_33_out, and_106_out, and_78_out);
  not not_35 (not_35_out, xor_54_out);
  not not_36 (not_36_out, xor_55_out);
  not not_37 (not_37_out, xor_56_out);
  not not_38 (not_38_out, xor_57_out);
  xor xor_66 (xor_69_out[3], xor_50_out, or_38_out);
  and and_113 (and_113_out, or_38_out, not_31_out);
  xor xor_67 (xor_69_out[2], xor_51_out, or_39_out);
  and and_114 (and_114_out, or_39_out, not_32_out);
  xor xor_68 (xor_69_out[1], xor_52_out, or_34_out);
  and and_115 (and_115_out, or_34_out, not_33_out);
  xor xor_69 (xor_69_out[0], xor_53_out, 1'b0);
  and and_116 (and_116_out, 1'b0, not_34_out);
  and and_117 (and_117_out, xnor_9_out, and_85_out);
  and and_118 (and_118_out, xnor_9_out, xnor_10_out, and_87_out);
  and and_119 (and_119_out, xnor_9_out, xnor_10_out, xnor_11_out, and_89_out);
  xor xor_70 (xor_69_out[7], xor_54_out, or_42_out);
  and and_120 (and_120_out, or_42_out, not_35_out);
  xor xor_71 (xor_69_out[6], xor_55_out, or_43_out);
  and and_121 (and_121_out, or_43_out, not_36_out);
  xor xor_72 (xor_69_out[5], xor_56_out, or_36_out);
  and and_122 (and_122_out, or_36_out, not_37_out);
  xor xor_73 (xor_69_out[4], xor_57_out, or_37_out);
  and and_123 (and_123_out, or_37_out, not_38_out);
  or or_34 (or_34_out, and_82_out, and_116_out);
  or or_35 (or_35_out, and_83_out, and_117_out, and_118_out, and_119_out);
  and and_124 (and_124_out, xnor_13_out, and_93_out);
  and and_125 (and_125_out, xnor_13_out, xnor_14_out, and_95_out);
  and and_126 (and_126_out, xnor_13_out, xnor_14_out, xnor_15_out, and_97_out);
  assign DATA_BUS_OUTPUT = buffer_48_out ? {d_ff_61_q[0], d_ff_61_q[7:1]} : 8'bz;  // Controlled_Buffer controlled_buffer_34
  assign DATA_BUS_OUTPUT = buffer_45_out ? {d_ff_61_q[6:0], d_ff_61_q[7]} : 8'bz;  // Controlled_Buffer controlled_buffer_35
  or or_36 (or_36_out, and_110_out, and_123_out);
  or or_37 (or_37_out, and_79_out, and_113_out);
  or or_38 (or_38_out, and_80_out, and_114_out);
  or or_39 (or_39_out, and_81_out, and_115_out);
  nor nor_1 (nor_1_out, and_111_out, or_35_out);
  or or_40 (or_40_out, and_91_out, and_124_out, and_125_out, and_126_out);
  assign DATA_BUS_OUTPUT = buffer_53_out ? xor_65_out : 8'bz;  // Controlled_Buffer controlled_buffer_36
  or or_41 (or_41_out, and_107_out, and_120_out);
  or or_42 (or_42_out, and_108_out, and_121_out);
  or or_43 (or_43_out, and_109_out, and_122_out);
  or or_44 (or_44_out, nor_1_out, and_127_out);
  and and_127 (and_127_out, and_111_out, nor_2_out);
  nor nor_2 (nor_2_out, and_112_out, or_40_out);
  or or_45 (or_45_out, buffer_48_out, buffer_45_out);
  assign DATA_BUS_OUTPUT = buffer_50_out ? xor_69_out : 8'bz;  // Controlled_Buffer controlled_buffer_37
  or or_46 (or_46_out, or_35_out, and_128_out);
  and and_128 (and_128_out, and_111_out, or_40_out);
  and and_129 (and_129_out, and_111_out, and_112_out);
  assign buffer_127_out = DATA_BUS_OUTPUT;  // Buffer buffer_127, 8 bits wide
  Pull_Resistor pull_resistor_80 (.node(buffer_127_out[7]));
  Pull_Resistor pull_resistor_81 (.node(buffer_127_out[6]));
  Pull_Resistor pull_resistor_82 (.node(buffer_127_out[5]));
  Pull_Resistor pull_resistor_83 (.node(buffer_127_out[4]));
  Pull_Resistor pull_resistor_84 (.node(buffer_127_out[3]));
  not not_39 (not_39_out, buffer_127_out[7]);
  not not_40 (not_40_out, buffer_127_out[6]);
  not not_41 (not_41_out, buffer_127_out[5]);
  not not_42 (not_42_out, buffer_127_out[4]);
  not not_43 (not_43_out, buffer_127_out[3]);
  and and_130 (and_130_out, not_39_out, not_40_out, not_41_out, not_42_out, not_43_out, not_44_out, not_45_out, not_46_out);
  Pull_Resistor pull_resistor_85 (.node(buffer_127_out[2]));
  Pull_Resistor pull_resistor_86 (.node(buffer_127_out[1]));
  Pull_Resistor pull_resistor_87 (.node(buffer_127_out[0]));
  not not_44 (not_44_out, buffer_127_out[2]);
  not not_45 (not_45_out, buffer_127_out[1]);
  not not_46 (not_46_out, buffer_127_out[0]);
  not not_47 (not_47_out, and_130_out);
  and and_131 (and_131_out, buffer_50_out, clock_in);
  and and_132 (and_132_out, buffer_53_out, clock_in);
  and and_133 (and_133_out, or_45_out, clock_in);
  and and_134 (and_134_out, buffer_41_out, clock_in);
  or or_47 (or_47_out, and_131_out, and_132_out, and_133_out);
  D_Flip_Flop d_ff_77 (.D(or_44_out), .clk(and_134_out), .Q(d_ff_83_q[6]), .reset(or_23_out));  // open: Qn, preset
  D_Flip_Flop d_ff_78 (.D(and_129_out), .clk(and_134_out), .Q(d_ff_83_q[5]), .reset(or_23_out));  // open: Qn, preset
  D_Flip_Flop d_ff_79 (.D(or_46_out), .clk(and_134_out), .Q(d_ff_83_q[4]), .reset(or_23_out));  // open: Qn, preset
  D_Flip_Flop d_ff_80 (.D(and_130_out), .clk(or_47_out), .Q(d_ff_83_q[3]), .reset(or_23_out));  // open: Qn, preset
  D_Flip_Flop d_ff_81 (.D(not_47_out), .clk(or_47_out), .Q(d_ff_83_q[2]), .reset(or_23_out));  // open: Qn, preset
  D_Flip_Flop d_ff_82 (.D(or_41_out), .clk(and_131_out), .Q(d_ff_83_q[1]), .reset(or_23_out));  // open: Qn, preset
  D_Flip_Flop d_ff_83 (.D(or_26_out), .clk(and_132_out), .Q(d_ff_83_q[0]), .reset(or_23_out));  // open: Qn, preset

  assign clock_out = clock_in;
  assign RAM_DATA_OUT = DATA_BUS_OUTPUT;
  assign tty_data_output = DATA_BUS_OUTPUT[6:0];

  // Notes on the sheet:
  //   PROGRAM COUNTER
  //   STEP COUNTER
  //   ADDRESS BUS
  //   STACK POINTER
  //   INSTRUCTION REGISTER
  //   STACK
  //   CONTROL LINES.
  //   20
  //   50
  //   30
  //   70
  //   DATA BUS
  //   CONTROL UNIT
  //   00
  //   10
  //   03
  //   02
  //   01
  //   00
  //   14
  //   12
  //   11
  //   10
  //   23
  //   22
  //   21
  //   20
  //   38
  //   37
  //   36
  //   15
  //   13
  //   35
  //   34
  //   33
  //   32
  //   31
  //   30
  //   51
  //   50
  //   7D
  //   7C
  //   7B
  //   7A
  //   79
  //   78
  //   77
  //   76
  //   75
  //   74
  //   73
  //   72
  //   71
  //   70
  //   A REGISTER
  //   B REGISTER
  //   LOGIC ENGINE
  //   ALU
  //   ADDER
  //   SUBTRACTOR
  //   COMPARATOR
  //   SHIFT/ROTATE RIGHT
  //   SHIFT/ROTATE LEFT
  //   ZERO FLAG UNIT
  //   FLAGS REGISTER
endmodule
